# Fritzing sketch odometer (saved by Fritzing 0.9.4)
circuit board: 4.6cm x 3.1cm
perfboards: 1

parts:
  Arduino_Nano = Arduino Nano (Rev3.0)
  R1 = Resistor [tolerance=±5% resistance=2k power=0.25 package=THT]
  R2 = Resistor [tolerance=±5% resistance=2k power=0.25 package=THT]
  R3 = Resistor [tolerance=±5% resistance=2k power=0.25 package=THT]
  R4 = Resistor [tolerance=±5% resistance=2k power=0.25 package=THT]
  JA1 = male pin header, 2 pins [form="♂ (male)" part_number=I2C_ADDR_J_1]
  JA2 = male pin header, 2 pins [form="♂ (male)" part_number=I2C_ADDR_J_2]
  JD1 = male pin header, 2 pins [form="♂ (male)" part_number=ENC_1_DIRECTION]
  JD2 = male pin header, 2 pins [form="♂ (male)" part_number=ENC_2_DIRECTION]
  I2C = male pin header, 4 pins [form="♂ (male)" part_number=Head_I2C]
  W = male pin header, 2 pins [form="♂ (male)" part_number=Head_Hall_White]
  Y = male pin header, 2 pins [form="♂ (male)" part_number="Head_Hall_Yellow (Interrupt)"]
  B = male pin header, 2 pins [form="♂ (male)" part_number=Head_Hall_GND]
  R = male pin header, 2 pins [form="♂ (male)" part_number=Head_Hall_5V]

nets:
  N1: Arduino_Nano.GND, JA1.pin2, JA2.pin2, JD1.pin2, JD2.pin2, I2C.pin3, B.pin1, B.pin2
  N2: Arduino_Nano.D2, R1.Pin_1, Y.pin2
  N3: Arduino_Nano.D3, R2.Pin_1, Y.pin1
  N4: Arduino_Nano.D4, R3.Pin_1, W.pin2
  N5: Arduino_Nano.D5, R4.Pin_1, W.pin1
  N6: Arduino_Nano.D6, JD1.pin1
  N7: Arduino_Nano.D7, JD2.pin1
  N8: Arduino_Nano.D11/MOSI, JA1.pin1
  N9: Arduino_Nano.D12/MISO, JA2.pin1
  N10: Arduino_Nano.5V, R1.Pin_0, R2.Pin_0, R3.Pin_0, R4.Pin_0, I2C.pin4, R.pin1, R.pin2
  N11: Arduino_Nano.A5, I2C.pin1
  N12: Arduino_Nano.A4, I2C.pin2

notes:
  Y
  R
  B
  U
  Hall
  5V
