# Fritzing sketch odometer (saved by Fritzing 0.9.3b)
circuit board: 6.5cm x 3cm
perfboards: 1

parts:
  Part1 = Arduino Nano (Rev3.0)
  R1 = Resistor [tolerance=±5% resistance=1k package=THT]
  R2 = Resistor [tolerance=±5% resistance=1k package=THT]
  R3 = Resistor [tolerance=±5% resistance=1k package=THT]
  R4 = Resistor [tolerance=±5% resistance=1k package=THT]
  J1 = male pin header, 2 pins [form="♂ (male)" part_number=I2C_ADDR_J_1]
  J2 = male pin header, 2 pins [form="♂ (male)" part_number=I2C_ADDR_J_2]
  J3 = male pin header, 2 pins [form="♂ (male)" part_number=ENC_1_DIRECTION]
  J4 = male pin header, 2 pins [form="♂ (male)" part_number=ENC_2_DIRECTION]
  J5 = male pin header, 4 pins [form="♂ (male)" part_number=Head_I2C]
  J6 = male pin header, 2 pins [form="♂ (male)" part_number=Head_Hall_Yellow]
  J7 = male pin header, 2 pins [form="♂ (male)" part_number="Head_Hall_White (Interrupt)"]
  J8 = male pin header, 2 pins [form="♂ (male)" part_number=Head_Hall_GND]
  J9 = male pin header, 2 pins [form="♂ (male)" part_number=Head_Hall_5V]

nets:
  N1: Part1.GND, J1.pin2, J2.pin2, J3.pin2, J4.pin2, J5.pin3, J8.pin1, J8.pin2
  N2: Part1.D2, R1.Pin_1, J7.pin2
  N3: Part1.D3, R2.Pin_1, J7.pin1
  N4: Part1.D4, R3.Pin_1, J6.pin2
  N5: Part1.D5, R4.Pin_1, J6.pin1
  N6: Part1.D6, J3.pin1
  N7: Part1.D7, J4.pin1
  N8: Part1.D11/MOSI, J1.pin1
  N9: Part1.D12/MISO, J2.pin1
  N10: Part1.5V, R1.Pin_0, R2.Pin_0, R3.Pin_0, R4.Pin_0, J5.pin4, J9.pin1, J9.pin2
  N11: Part1.A5, J5.pin1
  N12: Part1.A4, J5.pin2
